// Logisim project 8BIT_MINI_CPU.circ as structural Verilog: 1 circuit, main circuit main
module main (
  input  PC_INC_ENABLE,
  input  RESET,
  input  MAR_FROM_OPERAND,
  input  [7:0] DATA_IN_A,
  input  [7:0] DATA_IN_B,
  input  LOAD_B,
  input  LOAD_A,
  input  A_FROM_ALU,
  input  ALU_SUB,
  output [7:0] PC_OUT,
  output [7:0] MAR_OUT,
  output [7:0] RAM_DATA_OUT,
  output [7:0] MDR_OUT,
  output [3:0] OPCODE,
  output [3:0] OPERAND,
  output [7:0] OPERAND_8,
  output [7:0] B_VAL,
  output [7:0] A_VAL,
  output [7:0] ALU_RESULT_8_BIT,
  output ZERO_FLAG
);

  wire CLK_out;
  wire [7:0] adder_1_out, multiplexer_1_out, multiplexer_2_out, subtractor_1_out;

  Clock CLK (.out(CLK_out));
  Counter PC_8_Bit (
    .clr(RESET), .load(1'b0), .up(1'b1), .count(PC_INC_ENABLE), .clk(CLK_out), .D({8{1'b0}}), .Q(PC_OUT));  // open: carry
  Register MAR_8_Bit (.D(multiplexer_1_out), .en(1'b1), .clk(CLK_out), .Q(MAR_OUT), .clr(RESET));
  Multiplexer #(.width(8)) multiplexer_1 (
    .in0(PC_OUT), .in1(OPERAND_8), .out(multiplexer_1_out), .sel(MAR_FROM_OPERAND));
  Register REG_B (.D(DATA_IN_B), .en(LOAD_B), .clk(CLK_out), .Q(B_VAL), .clr(RESET));
  RAM RAM_256_x_8 (.addr(MAR_OUT), .we(1'b0), .oe(1'b1), .clk(CLK_out), .din({8{1'b0}}), .dout(RAM_DATA_OUT));
  Multiplexer #(.width(8)) multiplexer_2 (
    .in0(DATA_IN_A), .in1(ALU_RESULT_8_BIT), .out(multiplexer_2_out), .sel(A_FROM_ALU));
  Register MDR_8_Bit (.D(RAM_DATA_OUT), .en(1'b1), .clk(CLK_out), .Q(MDR_OUT), .clr(RESET));
  Register ACCUMULATOR_A (.D(multiplexer_2_out), .en(LOAD_A), .clk(CLK_out), .Q(A_VAL), .clr(RESET));
  Register IR_8_Bit (.D(MDR_OUT), .en(1'b1), .clk(CLK_out), .Q({OPERAND, OPCODE}), .clr(RESET));
  assign OPERAND_8 = {{4{1'b0}}, OPERAND};  // Bit_Extender bit_extender_1
  Adder adder_1 (.a(A_VAL), .b(B_VAL), .out(adder_1_out), .cin(1'b0));  // open: cout
  Subtractor subtractor_1 (.a(A_VAL), .b(B_VAL), .out(subtractor_1_out), .bin(1'b0));  // open: bout
  Multiplexer #(.width(8)) multiplexer_3 (
    .in0(adder_1_out), .in1(subtractor_1_out), .out(ALU_RESULT_8_BIT), .sel(ALU_SUB));
  Comparator #(.mode("unsigned")) comparator_1 (.a(ALU_RESULT_8_BIT), .b({8{1'b0}}), .eq(ZERO_FLAG));  // open: gt, lt

  // Notes on the sheet:
  //   [4] CONTROL
  //   [1] INSTRUCTION FETCH (PC -> MAR -> RAM -> MDR -> IR)
  //   [3] ARITHMETIC DATAPATH (A & B REGISTERS + ADD/SUB ALU)
  //   8-BIT MINI CPU ARCHITECTURE — INSTRUCTION FETCH & ARITHMETIC DATAPATH
  //   Pipeline: PC -> MAR -> RAM -> MDR -> IR -> Acc A / Reg B -> ALU (ADD / SUB)
  //   [2] INSTRUCTION DECODE
endmodule
